// Logisim project clock24hour.circ as structural Verilog: 1 circuit, main circuit main
module main (
);

  wire and_1_out, and_2_out, and_3_out, and_4_out, and_5_out, and_6_out, clock_1_out, or_1_out;
  wire [3:0] adder_1_out, adder_2_out, adder_3_out, adder_4_out, adder_5_out, adder_6_out, register_1_q,
       register_2_q, register_3_q, register_4_q, register_5_q, register_6_q;

  Register #(.width(4)) register_1 (.D(adder_1_out), .clk(or_1_out), .Q(register_1_q), .clr(and_2_out));  // open: en
  Adder #(.width(4)) adder_1 (.a(register_1_q), .b(4'b0001), .out(adder_1_out));  // open: cin, cout
  Adder #(.width(4)) adder_2 (.a(register_2_q), .b(4'b0001), .out(adder_2_out));  // open: cin, cout
  or or_1 (or_1_out, and_2_out, and_1_out);
  Register #(.width(4)) register_2 (.D(adder_2_out), .clk(and_3_out), .Q(register_2_q), .clr(or_1_out));  // open: en
  and and_1 (and_1_out, register_2_q[3], register_2_q[1]);
  and and_2 (and_2_out, register_2_q[2], register_1_q[1]);
  Hex_Digit_Display hex_digit_display_1 (.value(register_1_q));  // open: dp
  Hex_Digit_Display hex_digit_display_2 (.value(register_2_q));  // open: dp
  Register #(.width(4)) register_3 (.D(adder_3_out), .clk(and_4_out), .Q(register_3_q), .clr(and_3_out));  // open: en
  Adder #(.width(4)) adder_3 (.a(register_3_q), .b(4'b0001), .out(adder_3_out));  // open: cin, cout
  Hex_Digit_Display hex_digit_display_3 (.value(register_3_q));  // open: dp
  and and_3 (and_3_out, register_3_q[2], register_3_q[1]);
  Hex_Digit_Display hex_digit_display_4 (.value(register_4_q));  // open: dp
  Hex_Digit_Display hex_digit_display_5 (.value(register_5_q));  // open: dp
  Hex_Digit_Display hex_digit_display_6 (.value(register_6_q));  // open: dp
  Adder #(.width(4)) adder_4 (.a(register_4_q), .b(4'b0001), .out(adder_4_out));  // open: cin, cout
  Register #(.width(4)) register_4 (.D(adder_4_out), .clk(and_5_out), .Q(register_4_q), .clr(and_4_out));  // open: en
  and and_4 (and_4_out, register_4_q[3], register_4_q[1]);
  Adder #(.width(4)) adder_5 (.a(register_5_q), .b(4'b0001), .out(adder_5_out));  // open: cin, cout
  Register #(.width(4)) register_5 (.D(adder_5_out), .clk(and_6_out), .Q(register_5_q), .clr(and_5_out));  // open: en
  and and_5 (and_5_out, register_5_q[1], register_5_q[2]);
  Adder #(.width(4)) adder_6 (.a(register_6_q), .b(4'b0001), .out(adder_6_out));  // open: cin, cout
  Register #(.width(4)) register_6 (.D(adder_6_out), .clk(clock_1_out), .Q(register_6_q), .clr(and_6_out));  // open: en
  Clock clock_1 (.out(clock_1_out));
  and and_6 (and_6_out, register_6_q[3], register_6_q[1]);

  // Notes on the sheet:
  //   :
  //   :
endmodule
